# Fritzing sketch Schematic-Metereologic-Project (saved by Fritzing 1.0.4)
breadboards: 1

parts:
  Componente1 = Arduino Mega 2560 (Rev3)
  microSD1 = MicroSD Card Module
  ZS-042_RTC1 = ZS-042 RTC Module
  Capacitive_Soil_Moisture_Sensor1 = DFRobot Capacitive Soil Moisture Sensor V1.0 [part_number=SEN0193]
  DS18B1 = DS18B20 1-Wire Temperature Sensor Module [part_number=DS18B20]
  LCM1602_IIC1 = LCM1602 IIC [part_number="LCM1602 IIC" chip_label="LCM1602 IIC" package="DIP (Dual Inline) [THT]"]
  R3 = Resistor [tolerance=±5% power=0.25W resistance=220 package=THT]
  M1 = BME280
  LCD2 = 20x4 LCD display [part_number=2004A]
  S1 = Pushbutton [package="[THT]"]
  S2 = Pushbutton [package="[THT]"]
  S3 = Pushbutton [package="[THT]"]
  LED1 = LED - 5mm [color="Red (633nm)" current=0.030A package="5 mm [THT]"]  # not connected
  R4 = Resistor [tolerance=±5% power=0.25W resistance=220 package=THT]
  R5 = Resistor [tolerance=±5% power=0.25W resistance=220 package=THT]
  R6 = Resistor [tolerance=±5% power=0.25W resistance=220 package=THT]
  R7 = Resistor [tolerance=±5% power=0.25W resistance=220 package=THT]
  R8 = Resistor [tolerance=±5% power=0.25W resistance=220 package=THT]
  S4 = Pushbutton [package="[THT]"]
  R2 = Resistor [tolerance=±5% power=0.25W resistance=220 package=THT]
  R9 = Resistor [tolerance=±5% power=0.25W resistance=220 package=THT]

nets:
  N1: Componente1.A8, S1.Pin_1, S1.Pin_2, S2.Pin_1, S2.Pin_2, S3.Pin_1, S3.Pin_2, S4.Pin_1, S4.Pin_2, R9.Pin_1
  N2: Componente1.A9, M1.SDA
  N3: Componente1.A10, M1.SCL
  N4: Componente1.A11, ZS-042_RTC1.SDA
  N5: Componente1.A12, ZS-042_RTC1.SCL
  N6: Componente1.A13, LCM1602_IIC1.SDA
  N7: Componente1.A14, LCM1602_IIC1.SCL
  N8: Componente1.A15, Capacitive_Soil_Moisture_Sensor1.A
  N9: Componente1.D13_PWM, microSD1.SCK
  N10: Componente1.D12_PWM, microSD1.MISO
  N11: Componente1.D11_PWM, microSD1.MOSI
  N12: Componente1.D10_PWM, microSD1.CS
  N13: Componente1.D9_PWM, DS18B1.OUT, R3.Pin_1
  3V3: Componente1.3V3, M1.VIN
  VCC: Componente1.5V, microSD1.VCC, ZS-042_RTC1.VCC, Capacitive_Soil_Moisture_Sensor1.VCC, DS18B1.VDD, LCM1602_IIC1.VCC, R4.Pin_0, R2.Pin_1
  GND: Componente1.GND, microSD1.GND, ZS-042_RTC1.GND, Capacitive_Soil_Moisture_Sensor1.GND, DS18B1.GND, LCM1602_IIC1.GND, R3.Pin_0, M1.GND, R9.Pin_0
  VSS: LCM1602_IIC1.VSS, LCD2.Vss
  VDD: LCM1602_IIC1.VDD, LCD2.Vdd
  N14: LCM1602_IIC1.V0, LCD2.Vo
  N15: LCM1602_IIC1.RS, LCD2.RS
  N16: LCM1602_IIC1.RW, LCD2.R/W
  N17: LCM1602_IIC1.E, LCD2.E
  N18: LCM1602_IIC1.D0, LCD2.DB0
  N19: LCM1602_IIC1.D1, LCD2.DB1
  N20: LCM1602_IIC1.D2, LCD2.DB2
  N21: LCM1602_IIC1.D3, LCD2.DB3
  N22: LCM1602_IIC1.D4, LCD2.DB4
  N23: LCM1602_IIC1.D5, LCD2.DB5
  N24: LCM1602_IIC1.D6, LCD2.DB6
  N25: LCM1602_IIC1.D7, LCD2.DB7
  N26: LCM1602_IIC1.A, LCD2.A_+
  N27: LCM1602_IIC1.K, LCD2.K_-
  N28: LCM1602_IIC1.LED_A, LCM1602_IIC1.LED_B
  N29: S1.Pin_3, S1.Pin_4, R4.Pin_1, R5.Pin_0
  N30: S2.Pin_3, S2.Pin_4, R5.Pin_1, R6.Pin_0
  N31: S3.Pin_3, S3.Pin_4, R6.Pin_1, R7.Pin_0
  N32: R7.Pin_1, R8.Pin_0, S4.Pin_3, S4.Pin_4

custom parts:
  DFRobot Capacitive Soil Moisture Sensor V1.0: DFRobot Capacitive Soil Moisture Sensor V1.0 This product measures soil moisture levels by capacitive sensing, rather than resistive sensing like other types of moisture sensor. It is made of a corrosion resistant material giving it a long service life. Insert it into soil and impress your friends with the real-time soil moisture data! The product includes an on-board voltage regulator which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
  DS18B20 1-Wire Temperature Sensor Module: DS18B20 1-Wire Temperature Sensor Module The DS18B20 digital thermometer provides 9-bit to 12-bit Celsius temperature measurements and has an alarm function with nonvolatile user-programmable upper and lower trigger points. The DS18B20 communicates over a 1-Wire bus that by definition requires only one data line (and ground) for communication with a central microprocessor. In addition, the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
  LCM1602 IIC: I2C-Module to use a 1602 or 2004 LCD on with the wire.h libory Serial LCD Modul
  BME280: Temperature Humidity Barometric presure Sensor
  20x4 LCD display: 20x4 character display. CHECK LED POLARITY BEFORE CONNECTING POWER Some versions of the dispaly have the polarity of the LED pins "A" and "K" reversed.
